# Fritzing sketch wheelChair (saved by Fritzing 0.9.3b)
breadboards: 1

parts:
  Part1 = Arduino Uno (Rev3)
  M1 = DC Motor
  M2 = DC Motor
  hc-sr1 = hc-sr04
  Part2 = Bluetooth HC-05 Macho
  S1 = H-Bridge with L298N
  BAT1 = Battery Holders [package=lipo-1100mAh]  # not connected
  LED2 = LED - 5mm [color="Green (570nm)" package="5 mm [THT]"]
  hc-sr2 = hc-sr04
  J1 = Piezo Speaker
  S2 = Square Pushbutton

nets:
  N1: Part1.D8, S1.IN1
  N2: Part1.D9_PWM, S1.IN2
  N3: Part1.D10_PWM/SS, S1.IN3
  N4: Part1.D11_PWM/MOSI, S1.IN4
  N5: Part1.D12/MISO, hc-sr1.Trig
  N6: Part1.D13/SCK, hc-sr1.Echo
  N7: Part1.D0/RX, Part2.TXD
  N8: Part1.D1/TX, Part2.RXD
  N9: Part1.D3_PWM, S2.leg0
  N10: Part1.D4, J1.pin2
  N11: Part1.D5_PWM, LED2.anode
  N12: Part1.D6_PWM, hc-sr2.Echo
  N13: Part1.D7, hc-sr2.Trig
  VCC: Part1.5V, hc-sr1.VCC, Part2.VCC, hc-sr2.VCC
  GND: Part1.GND, hc-sr1.GND, Part2.GND, S1.GND, LED2.cathode, hc-sr2.GND, J1.pin1, S2.leg1
  VIN: Part1.VIN, S1.5V
  N14: M1.pin_1, S1.M1-02
  N15: M1.pin_2, S1.M1-01
  N16: M2.pin_1, S1.M2-02
  N17: M2.pin_2, S1.M2-01

notes:
  Right Motor
  Left Motor
  Arduino
  Motor Driver
  Lipo Battery
  Bluetooth Module
  Ultrasonic Sensor
  Breadboard
  LED
  Push Button
  Buzzer

custom parts:
  H-Bridge with L298N: h-bridge
